// Logisim project Lab3_Procesador_Monociclo.circ as structural Verilog: 4 circuits, main circuit main
module main (
);

  wire [31:0] ifetch_1_instruction;

  IFetch ifetch_1 (.Instruction(ifetch_1_instruction));  // open: nextPC, CLK, Reset, PCplus4
  ISplit isplit_1 (.Instruction(ifetch_1_instruction));  // open: immediate, address, funct, shamt, rd, rt, rs, opcode
  RegFile regfile_1 ();  // open: ReadReg1, ReadReg2, WriteRegister, WriteData, CLK, RegWrite, Reset, ReadData2, ReadData1
endmodule

module IFetch (
  input  [31:0] nextPC,
  input  CLK,
  input  Reset,
  output [31:0] PCplus4,
  output [31:0] Instruction
);

  wire [1:0] register_1_q, register_1_q_2, register_1_q_3, register_1_q_4, register_1_q_5, register_1_q_6,
       register_1_q_7, register_1_q_8, register_1_q_9, register_1_q_10, register_1_q_11, register_1_q_12,
       register_1_q_13, register_1_q_14, register_1_q_15, register_1_q_16;

  Register #(.width(32)) register_1 (
    .D(nextPC), .clk(CLK),
    .Q({register_1_q_8, register_1_q_7, register_1_q_6, register_1_q_5, register_1_q_4, register_1_q_3, register_1_q_2, register_1_q_16, register_1_q_15, register_1_q_14, register_1_q_13, register_1_q_12, register_1_q_11, register_1_q_10, register_1_q_9, register_1_q}),
    .clr(Reset));  // open: en
  Adder #(.width(32)) adder_1 (
    .a(32'h4),
    .b({register_1_q_8, register_1_q_7, register_1_q_6, register_1_q_5, register_1_q_4, register_1_q_3, register_1_q_2, register_1_q_16, register_1_q_15, register_1_q_14, register_1_q_13, register_1_q_12, register_1_q_11, register_1_q_10, register_1_q_9, register_1_q}),
    .out(PCplus4));  // open: cin, cout
  ROM #(.addrWidth(16), .dataWidth(32)) rom_1 (
    .addr({register_1_q_16, register_1_q_15, register_1_q_14, register_1_q_13, register_1_q_12, register_1_q_11, register_1_q_10, register_1_q_9}),
    .data(Instruction));
endmodule

module ISplit (
  input  [31:0] Instruction,
  output [15:0] immediate,
  output [25:0] address,
  output [5:0] funct,
  output [4:0] shamt,
  output [4:0] rd,
  output [4:0] rt,
  output [4:0] rs,
  output [5:0] opcode
);


  assign address = Instruction[25:0];
  assign funct = Instruction[5:0];
  assign immediate = Instruction[15:0];
  assign opcode = Instruction[31:26];
  assign rd = Instruction[15:11];
  assign rs = Instruction[25:21];
  assign rt = Instruction[20:16];
  assign shamt = Instruction[10:6];
endmodule

module RegFile (
  input  RegWrite,
  input  [4:0] ReadReg1,
  input  [4:0] ReadReg2,
  input  [4:0] WriteRegister,
  input  [31:0] WriteData,
  input  CLK,
  input  Reset,
  output [31:0] ReadData1,
  output [31:0] ReadData2
);

  wire decoder_1_out0, decoder_1_out1, decoder_1_out2, decoder_1_out3, decoder_1_out4, decoder_1_out5,
       decoder_1_out6, decoder_1_out7, decoder_1_out8, decoder_1_out9, decoder_1_out10, decoder_1_out11,
       decoder_1_out12, decoder_1_out13, decoder_1_out14, decoder_1_out15, decoder_1_out16, decoder_1_out17,
       decoder_1_out18, decoder_1_out19, decoder_1_out20, decoder_1_out21, decoder_1_out22, decoder_1_out23,
       decoder_1_out24, decoder_1_out25, decoder_1_out26, decoder_1_out27, decoder_1_out28, decoder_1_out29,
       decoder_1_out30, decoder_1_out31;
  wire [31:0] a0_q, a1_q, a2_q, a3_q, at_q, fp_q, gp_q, k0_q, k1_q, ra_q, s0_q, s1_q, s2_q, s3_q, s4_q, s5_q,
       s6_q, s7_q, sp_q, t0_q, t1_q, t2_q, t3_q, t4_q, t5_q, t6_q, t7_q, t8_q, t9_q, v0_q, v1_q, zero_q;

  Register #(.width(32)) a0 (.D(WriteData), .en(decoder_1_out4), .clk(CLK), .Q(a0_q), .clr(Reset));
  Register #(.width(32)) v1 (.D(WriteData), .en(decoder_1_out3), .clk(CLK), .Q(v1_q), .clr(Reset));
  Register #(.width(32)) v0 (.D(WriteData), .en(decoder_1_out2), .clk(CLK), .Q(v0_q), .clr(Reset));
  Register #(.width(32)) at (.D(WriteData), .en(decoder_1_out1), .clk(CLK), .Q(at_q), .clr(Reset));
  Register #(.width(32)) zero (.D(WriteData), .en(decoder_1_out0), .clk(CLK), .Q(zero_q), .clr(Reset));
  Register #(.width(32)) t1 (.D(WriteData), .en(decoder_1_out9), .clk(CLK), .Q(t1_q), .clr(Reset));
  Register #(.width(32)) t0 (.D(WriteData), .en(decoder_1_out8), .clk(CLK), .Q(t0_q), .clr(Reset));
  Register #(.width(32)) a3 (.D(WriteData), .en(decoder_1_out7), .clk(CLK), .Q(a3_q), .clr(Reset));
  Register #(.width(32)) a2 (.D(WriteData), .en(decoder_1_out6), .clk(CLK), .Q(a2_q), .clr(Reset));
  Register #(.width(32)) a1 (.D(WriteData), .en(decoder_1_out5), .clk(CLK), .Q(a1_q), .clr(Reset));
  Decoder #(.select(5)) decoder_1 (
    .out0(decoder_1_out0), .out1(decoder_1_out1), .out2(decoder_1_out2), .out3(decoder_1_out3),
    .out4(decoder_1_out4), .out5(decoder_1_out5), .out6(decoder_1_out6), .out7(decoder_1_out7),
    .out8(decoder_1_out8), .out9(decoder_1_out9), .out10(decoder_1_out10), .out11(decoder_1_out11),
    .out12(decoder_1_out12), .out13(decoder_1_out13), .out14(decoder_1_out14), .out15(decoder_1_out15),
    .out16(decoder_1_out16), .out17(decoder_1_out17), .out18(decoder_1_out18), .out19(decoder_1_out19),
    .out20(decoder_1_out20), .out21(decoder_1_out21), .out22(decoder_1_out22), .out23(decoder_1_out23),
    .out24(decoder_1_out24), .out25(decoder_1_out25), .out26(decoder_1_out26), .out27(decoder_1_out27),
    .out28(decoder_1_out28), .out29(decoder_1_out29), .out30(decoder_1_out30), .out31(decoder_1_out31),
    .sel(WriteRegister), .en(RegWrite));
  Register #(.width(32)) t6 (.D(WriteData), .en(decoder_1_out14), .clk(CLK), .Q(t6_q), .clr(Reset));
  Register #(.width(32)) t5 (.D(WriteData), .en(decoder_1_out13), .clk(CLK), .Q(t5_q), .clr(Reset));
  Register #(.width(32)) t4 (.D(WriteData), .en(decoder_1_out12), .clk(CLK), .Q(t4_q), .clr(Reset));
  Register #(.width(32)) t3 (.D(WriteData), .en(decoder_1_out11), .clk(CLK), .Q(t3_q), .clr(Reset));
  Register #(.width(32)) t2 (.D(WriteData), .en(decoder_1_out10), .clk(CLK), .Q(t2_q), .clr(Reset));
  Register #(.width(32)) s1 (.D(WriteData), .en(decoder_1_out19), .clk(CLK), .Q(s1_q), .clr(Reset));
  Register #(.width(32)) s0 (.D(WriteData), .en(decoder_1_out18), .clk(CLK), .Q(s0_q), .clr(Reset));
  Register #(.width(32)) t9 (.D(WriteData), .en(decoder_1_out17), .clk(CLK), .Q(t9_q), .clr(Reset));
  Register #(.width(32)) t8 (.D(WriteData), .en(decoder_1_out16), .clk(CLK), .Q(t8_q), .clr(Reset));
  Register #(.width(32)) t7 (.D(WriteData), .en(decoder_1_out15), .clk(CLK), .Q(t7_q), .clr(Reset));
  Register #(.width(32)) s6 (.D(WriteData), .en(decoder_1_out24), .clk(CLK), .Q(s6_q), .clr(Reset));
  Register #(.width(32)) s5 (.D(WriteData), .en(decoder_1_out23), .clk(CLK), .Q(s5_q), .clr(Reset));
  Register #(.width(32)) s4 (.D(WriteData), .en(decoder_1_out22), .clk(CLK), .Q(s4_q), .clr(Reset));
  Register #(.width(32)) s3 (.D(WriteData), .en(decoder_1_out21), .clk(CLK), .Q(s3_q), .clr(Reset));
  Register #(.width(32)) s2 (.D(WriteData), .en(decoder_1_out20), .clk(CLK), .Q(s2_q), .clr(Reset));
  Register #(.width(32)) sp (.D(WriteData), .en(decoder_1_out29), .clk(CLK), .Q(sp_q), .clr(Reset));
  Register #(.width(32)) gp (.D(WriteData), .en(decoder_1_out28), .clk(CLK), .Q(gp_q), .clr(Reset));
  Register #(.width(32)) k1 (.D(WriteData), .en(decoder_1_out27), .clk(CLK), .Q(k1_q), .clr(Reset));
  Register #(.width(32)) k0 (.D(WriteData), .en(decoder_1_out26), .clk(CLK), .Q(k0_q), .clr(Reset));
  Register #(.width(32)) s7 (.D(WriteData), .en(decoder_1_out25), .clk(CLK), .Q(s7_q), .clr(Reset));
  Register #(.width(32)) ra (.D(WriteData), .en(decoder_1_out31), .clk(CLK), .Q(ra_q), .clr(Reset));
  Register #(.width(32)) fp (.D(WriteData), .en(decoder_1_out30), .clk(CLK), .Q(fp_q), .clr(Reset));
  Multiplexer #(.select(5), .width(32)) multiplexer_1 (
    .out(ReadData1), .sel(ReadReg1));  // open: in0, in1, in2, in3, in4, in5, in6, in7, in8, in9, in10, in11, in12, in13, in14, in15, in16, in17, in18, in19, in20, in21, in22, in23, in24, in25, in26, in27, in28, in29, in30, in31
  Multiplexer #(.select(5), .width(32)) multiplexer_2 (
    .out(ReadData2), .sel(ReadReg2));  // open: in0, in1, in2, in3, in4, in5, in6, in7, in8, in9, in10, in11, in12, in13, in14, in15, in16, in17, in18, in19, in20, in21, in22, in23, in24, in25, in26, in27, in28, in29, in30, in31

  // Other names for the same wires on the sheet: rr1[4:0] = ReadReg1; rr2[4:0] = ReadReg2; wd[31:0] = WriteData
endmodule
